# Fritzing sketch weasley_clock (saved by Fritzing 1.0.6)

parts:
  Raspberry_Pi = Raspberry Pi 2
  Adafruit_Pixel_Shifter1 = Adafruit Pixel Shifter [mn=Adafruit mpn=#6066 part_number=#6066]
  Bauteil1 = Quarter 60 NeoPixel Ring [part_number=1768]
  Bauteil2 = Quarter 60 NeoPixel Ring [part_number=1768]
  Bauteil4 = Quarter 60 NeoPixel Ring [part_number=1768]
  5V_/_3_6A = 2.1mm Barrel Jack with Terminal Block
  Privacy_Switch = Toggle Switch [package=THT]
  1000µF_6_3V = Electrolytic Capacitor [package="100 mil [THT, electrolytic]"]
  NeoPixel_Ring_/_Clockface = Quarter 60 NeoPixel Ring [part_number=1768]

nets:
  3V3: Raspberry_Pi.3v3, Adafruit_Pixel_Shifter1.VIN
  N1: Raspberry_Pi.GPIO4, Privacy_Switch.COM
  GND: Raspberry_Pi.GND, Adafruit_Pixel_Shifter1.GND, Bauteil1.GND, Bauteil2.GND, Bauteil4.GND, 5V_/_3_6A.NEG, Privacy_Switch.L1, 1000µF_6_3V.-, NeoPixel_Ring_/_Clockface.GND
  N2: Raspberry_Pi.GPIO18, Adafruit_Pixel_Shifter1.DAT_3V
  N3: Adafruit_Pixel_Shifter1.DAT_5V, NeoPixel_Ring_/_Clockface.DATAIN
  VDD: Bauteil1.VDD, Bauteil2.VDD, Bauteil4.VDD, 5V_/_3_6A.POS, 1000µF_6_3V.+, NeoPixel_Ring_/_Clockface.VDD
  N4: Bauteil1.DATAIN, NeoPixel_Ring_/_Clockface.DATAOUT
  N5: Bauteil1.DATAOUT, Bauteil2.DATAIN
  N6: Bauteil2.DATAOUT, Bauteil4.DATAIN

custom parts:
  Quarter 60 NeoPixel Ring: The biggest NeoPixel Ring yet! With four of these you can make a huge ring with 60 ultra bright smart LED NeoPixels are arranged in a circle with a 6.2" diameter. The rings are 'chainable' - connect the output pin of one to the input pin of another. Use only one microcontroller pin to control as many as you can chain together!
  Electrolytic Capacitor: A small electrolytic capacitor
